# Fritzing sketch led_volleyball_wire (saved by Fritzing 0.9.9b)

parts:
  Part1 = Arduino Nano (Rev3.0) (ICSP)
  U2 = WS2812 RGB LED strip
  Part2 = IR Receiver Breakout [package=PCB]
  C1 = Capacitor Polarized [package=cpol-radial-1000uf-25v]
  JACK1 = 2.1mm_Barrel_Jack_with_Terminal_Block

nets:
  N1: Part1.D6, Part2.GND
  N2: U2.GND, C1.+, JACK1.connector1
  N3: U2.VCC, C1.-

custom parts:
  WS2812 RGB LED strip: WS2812 strip
