# Fritzing sketch brushinator_5k (saved by Fritzing 0.9.9b)

parts:
  Part1 = Arduino Nano (Rev3.0)
  16_LED_Ring = 16 NeoPixel Ring [part_number=1463]
  Part2 = Adafruit APDS-9960 [part_number="Adafruit #3595"]

nets (from the breadboard view):
  GND: Part1.GND, 16_LED_Ring.GND, Part2.GND
  N1: Part1.D2, Part2.INT
  N2: Part1.D6, 16_LED_Ring.OUT
  5V: Part1.5V, 16_LED_Ring.VDD
  N3: Part1.A5, Part2.SCL
  N4: Part1.A4, Part2.SDA
  3V3: Part1.3V3, Part2.3.3V

custom parts:
  16 NeoPixel Ring: 16 ultra bright smart LED NeoPixels are arranged in a circle with 1.75" (44.5mm) outer diameter. The rings are 'chainable' - connect the output pin of one to the input pin of another. Use only one microcontroller pin to control as many as you can chain together! Each LED is addressable as the driver chip is inside the LED. Each one has ~18mA constant current drive so the color will be very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
  Adafruit APDS-9960: The APDS9960 from Avago Technologies has an integrated IR LED and driver, along with four directional photodiodes that sense reflected IR energy from the LED. It's proximity detection feature allows it to measure the distance an object is from the front of the sensor (up to a few centimeters) with 8 bit resolution. Since there are four IR sensors, you can measure the changes in light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
