# Fritzing sketch led_volleyball_wire (saved by Fritzing 0.9.9b)
breadboards: 1

parts:
  Part1 = Arduino Nano (Rev3.0) (ICSP)
  U2 = WS2812 RGB LED strip
  Part2 = IR Receiver Breakout [package=PCB]
  JACK1 = 2.1mm Barrel Jack with Terminal Block
  C1 = Electrolytic Capacitor [capacitance=10μF voltage=35V package="0605 [SMD, electrolytic]"]

nets:
  N1: Part1.D2, U2.DIN
  N2: Part1.D6, Part2.OUT
  GND: Part1.GND, U2.GND, Part2.GND, JACK1.NEG, C1.-
  VCC: Part1.5V, U2.VCC, Part2.VCC, JACK1.POS, C1.+

custom parts:
  WS2812 RGB LED strip: WS2812 strip
