# Fritzing sketch smart_bbq_controller (saved by Fritzing 0.9.9b)

parts:
  Part1 = Arduino Motor Shield (Rev3)
  JACK1 = 2.1mm Barrel Jack with Terminal Block
  Part2 = Adafruit Thermocouple Amplifier MAX31855 [part_number="Adafruit #269"]
  M1 = Stepper Motor - Bipolar
  LCD1 = LCD screen  # not connected
  DS1 = DS18B20 1-Wire Temperature Sensor Probe Cable  # not connected

nets:
  N1: Part1.D3_PWM/A, Part2.DO
  N2: Part1.D4, Part2.CS
  N3: Part1.D5_PWM, Part2.CLK
  N4: Part1.B-, M1.D
  N5: Part1.B+, M1.B
  N6: Part1.A-, M1.C
  N7: Part1.A+, M1.A
  N8: Part1.VMOT, JACK1.NEG
  GND: Part1.GND, JACK1.POS, Part2.GND
  5V: Part1.5V, Part2.+3V3

notes:
  Note the ordering of the wires for the Adafruit Stepper Motor

custom parts:
  Adafruit Thermocouple Amplifier MAX31855: Thermocouples are very sensitive, requiring a good amplifier with a cold-compensation reference. The MAX31855K does everything for you, and can be easily interfaced with any microcontroller, even one without an analog input. This breakout board has the chip itself, a 3.3V regulator with 10uF bypass capacitors and level shifting circuitry, all assembled and tested. Comes with a 2 pin terminal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
